// Digital circuit Address Decoder chips.dig as structural Verilog
module Address_Decoder_chips (
  input  E,
  input  R_nW,
  input  A15,
  input  A14,
  input  A13,
  input  A12,
  input  A11,
  input  A10,
  output nBOOT,
  output nSPARE,
  output nEXTRA,
  output nRAM,
  output nPIA1,
  output nPIA2,
  output out_15,
  output out_16,
  output out_17,
  output out_18,
  output RDIO,
  output WRIO,
  output out_21
);

  wire _74138_1_pin7, _74138_1_pin9, _74138_1_pin10, _74138_1_pin11, _74138_1_pin12, _74138_1_pin13,
       _74138_1_pin14, _74138_1_pin15, _74138_2_pin12, _74138_2_pin13, not_1_out;

  not not_1 (not_1_out, R_nW);
  _74138 _74138_1 (
    .pin1(A13), .pin2(A14), .pin3(A15), .pin4(1'b0), .pin5(1'b0), .pin6(E), .pin7(_74138_1_pin7),
    .pin8(1'b0), .pin9(_74138_1_pin9), .pin10(_74138_1_pin10), .pin11(_74138_1_pin11),
    .pin12(_74138_1_pin12), .pin13(_74138_1_pin13), .pin14(_74138_1_pin14), .pin15(_74138_1_pin15),
    .pin16(1'b1));
  _74138 _74138_2 (
    .pin1(A10), .pin2(A11), .pin3(A12), .pin4(_74138_1_pin10), .pin5(_74138_1_pin10), .pin6(E),
    .pin7(out_18), .pin8(1'b0), .pin9(out_17), .pin10(out_16), .pin11(out_15), .pin12(_74138_2_pin12),
    .pin13(_74138_2_pin13), .pin14(nPIA2), .pin15(nPIA1), .pin16(1'b1));
  or or_1 (WRIO, _74138_2_pin12, R_nW);
  _7421 _7421_1 (
    .pin1(_74138_1_pin15), .pin2(_74138_1_pin14), .pin4(_74138_1_pin13), .pin5(_74138_1_pin12), .pin6(nRAM),
    .pin7(1'b0), .pin8(out_21), .pin9(1'b0), .pin10(1'b0), .pin12(1'b0), .pin13(1'b0), .pin14(1'b1));  // open: pin3, pin11
  _7432 _7432_1 (
    .pin1(not_1_out), .pin2(_74138_1_pin7), .pin3(nBOOT), .pin4(not_1_out), .pin5(_74138_1_pin9),
    .pin6(nSPARE), .pin7(1'b0), .pin8(nEXTRA), .pin9(not_1_out), .pin10(_74138_1_pin11), .pin11(RDIO),
    .pin12(not_1_out), .pin13(_74138_2_pin13), .pin14(1'b1));

  // Notes on the sheet:
  //   E: Enable
  //   R_nW: Read Not Write
  //   nBOOT: $E000
  //   nSPARE: $C000
  //   nRAM: $0000
endmodule

/* Test case RAM CS:
E R/~W A15 A14 A13 ~RAM

 0  X   X  X   X   1
 1  X   1  X   X   1
 1  X   0  X   X   0
 
*/

/* Test case BOOT CS:
E R/~W A15 A14 A13 ~BOOT

 0   X   X  X  X   1
 1   0   X  X  X   1
 1   1   0  X  X   1
 1   1   1  0  0   1
 1   1   1  0  1   1
 1   1   1  1  0   1
 1   1   1  1  1   0
  
*/

/* Test case SPARE CS:
E R/~W A15 A14 A13 ~SPARE

 0   X   X  X  X   1
 1   0   X  X  X   1
 1   1   0  X  X   1
 1   1   1  0  0   1
 1   1   1  0  1   1
 1   1   1  1  0   0
 1   1   1  1  1   1
  
*/

/* Test case EXTRA CS:
E R/~W A15 A14 A13 ~EXTRA

 0   X   X  X  X   1
 1   0   X  X  X   1
 1   1   0  X  X   1
 1   1   1  0  0   0
 1   1   1  0  1   1
 1   1   1  1  0   1
 1   1   1  1  1   1
  
*/
